// Logisim project circuito_completo_8bits.circ as structural Verilog: 19 circuits, main circuit main
module main (
);

  wire D_adr, flags_caez_1_a, flags_caez_1_c, flags_caez_1_e, flags_caez_1_z, I_O, IO_e, IO_s,
       keyboard_control_1_out_8, keyboard_control_1_out_9, monitor_control_1_monitor_set,
       monitor_control_1_monitor_write_enable, or_1_out, uc_1_acc_e, uc_1_acc_s, uc_1_bus_1, uc_1_flags_s,
       uc_1_iar_e, uc_1_iar_s, uc_1_init, uc_1_ir_s, uc_1_mar_s, uc_1_r0_e, uc_1_r0_s, uc_1_r1_e, uc_1_r1_s,
       uc_1_r2_e, uc_1_r2_s, uc_1_r3_e, uc_1_r3_s, uc_1_ram_e, uc_1_ram_s, uc_1_tmp_s, ula_1_a_larger,
       ula_1_c_out, ula_1_equal, ula_1_zero;
  wire [2:0] uc_1_sel_ula;
  wire [6:0] keyboard_1_data, monitor_control_1_data_monitor;
  wire [7:0] ACC_q, controlled_buffer_1_out, IAR_q, IR_q, MAR_q, multiplexer_1_out, R0_q, R1_q, R2_q, R3_q,
       TMP_q, ula_1_acc;

  Register TMP (.D(controlled_buffer_1_out), .Q(TMP_q), .clk(uc_1_tmp_s));  // open: en, clr
  Multiplexer #(.width(8)) multiplexer_1 (.in0(TMP_q), .in1(8'h1), .out(multiplexer_1_out), .sel(uc_1_bus_1));
  ULA ula_1 (
    .EntA_ULA(controlled_buffer_1_out), .EntB_ULA(multiplexer_1_out), .ACC(ula_1_acc),
    .Sel_ULA(uc_1_sel_ula), .Bus_1(uc_1_bus_1), .C_in(flags_caez_1_c), .C_out(ula_1_c_out),
    .a_larger(ula_1_a_larger), .equal(ula_1_equal), .zero(ula_1_zero));
  Register ACC (.D(ula_1_acc), .Q(ACC_q), .clk(uc_1_acc_s));  // open: en, clr
  Flags_Caez flags_caez_1 (
    .C_out(ula_1_c_out), .a_larger(ula_1_a_larger), .equal(ula_1_equal), .zero(ula_1_zero),
    .Flags_s(uc_1_flags_s), .C(flags_caez_1_c), .A(flags_caez_1_a), .E(flags_caez_1_e), .Z(flags_caez_1_z));
  assign controlled_buffer_1_out = uc_1_acc_e ? ACC_q : 8'bz;  // Controlled_Buffer controlled_buffer_1
  assign controlled_buffer_1_out = uc_1_r0_e ? R0_q : 8'bz;  // Controlled_Buffer controlled_buffer_2
  Register R0 (.D(controlled_buffer_1_out), .Q(R0_q), .clk(uc_1_r0_s));  // open: en, clr
  Keyboard keyboard_1 (
    .clk(keyboard_control_1_out_8), .re(keyboard_control_1_out_9), .data(keyboard_1_data));  // open: clr, avail
  keyboard_control keyboard_control_1 (
    .in_1(controlled_buffer_1_out), .init(IO_e), .key(keyboard_1_data), .IO_s(IO_s), .O_A(D_adr), .I_O(I_O),
    .out_7(controlled_buffer_1_out), .out_8(keyboard_control_1_out_8), .out_9(keyboard_control_1_out_9));
  Register R1 (.D(controlled_buffer_1_out), .Q(R1_q), .clk(uc_1_r1_s));  // open: en, clr
  assign controlled_buffer_1_out = uc_1_r1_e ? R1_q : 8'bz;  // Controlled_Buffer controlled_buffer_3
  Register IAR (.D(controlled_buffer_1_out), .Q(IAR_q), .clk(uc_1_iar_s));  // open: en, clr
  assign controlled_buffer_1_out = uc_1_iar_e ? IAR_q : 8'bz;  // Controlled_Buffer controlled_buffer_4
  assign controlled_buffer_1_out = uc_1_r2_e ? R2_q : 8'bz;  // Controlled_Buffer controlled_buffer_5
  Register R2 (.D(controlled_buffer_1_out), .Q(R2_q), .clk(uc_1_r2_s));  // open: en, clr
  LED led_1 (.in(uc_1_init));
  UC uc_1 (
    .Sel_ULA(uc_1_sel_ula), .carry_out(flags_caez_1_c), .a_larger(flags_caez_1_a), .equal(flags_caez_1_e),
    .zero(flags_caez_1_z), .Bus_1(uc_1_bus_1), .TMP_s(uc_1_tmp_s), .R0_s(uc_1_r0_s), .R0_e(uc_1_r0_e),
    .R1_s(uc_1_r1_s), .R1_e(uc_1_r1_e), .R2_s(uc_1_r2_s), .R2_e(uc_1_r2_e), .R3_s(uc_1_r3_s),
    .R3_e(uc_1_r3_e), .MAR_s(uc_1_mar_s), .Flags_s(uc_1_flags_s), .ACC_s(uc_1_acc_s), .ACC_e(uc_1_acc_e),
    .IAR_s(uc_1_iar_s), .IAR_e(uc_1_iar_e), .IR_s(uc_1_ir_s), .Ent_IR(IR_q), .IO_s(IO_s), .IO_e(IO_e),
    .Data_adress(D_adr), .Input_Output(I_O), .RAM_e(uc_1_ram_e), .RAM_s(uc_1_ram_s), .Init(uc_1_init));
  Register IR (.D(controlled_buffer_1_out), .Q(IR_q), .clk(uc_1_ir_s));  // open: en, clr
  Monitor_control monitor_control_1 (
    .IO_s(IO_s), .D_adr(D_adr), .I_O(I_O), .Data_Output(controlled_buffer_1_out),
    .Data_Monitor(monitor_control_1_data_monitor), .Monitor_set(monitor_control_1_monitor_set),
    .Monitor_write_enable(monitor_control_1_monitor_write_enable));
  Register R3 (.D(controlled_buffer_1_out), .Q(R3_q), .clk(uc_1_r3_s));  // open: en, clr
  assign controlled_buffer_1_out = uc_1_r3_e ? R3_q : 8'bz;  // Controlled_Buffer controlled_buffer_6
  TTY tty_1 (
    .data(monitor_control_1_data_monitor), .clk(monitor_control_1_monitor_set),
    .we(monitor_control_1_monitor_write_enable));  // open: clr
  or or_1 (or_1_out, uc_1_ram_s, uc_1_ram_e);
  RAM #(.databus("bidir")) ram_1 (
    .addr(MAR_q), .we(uc_1_ram_s), .oe(uc_1_ram_e), .clk(or_1_out), .data(controlled_buffer_1_out));
  Register MAR (.D(controlled_buffer_1_out), .Q(MAR_q), .clk(uc_1_mar_s));  // open: en, clr

  // Notes on the sheet:
  //   Bus_1
  //   ALUNO: WASHNGTON ANTÔNIO MORENO RIEGA - 22152254 
  //   TURMA: CB01
endmodule

module Sum1 (
  input  C__In,
  input  Bit_A,
  input  Bit_B,
  output soma,
  output C__Out
);

  wire and_1_out, and_2_out, xor_1_out;

  xor xor_1 (xor_1_out, Bit_A, Bit_B);
  and and_1 (and_1_out, Bit_A, Bit_B);
  and and_2 (and_2_out, xor_1_out, C__In);
  xor xor_2 (soma, xor_1_out, C__In);
  or or_1 (C__Out, and_2_out, and_1_out);
endmodule

// soma
module Sum8 (
  input  C__In,
  input  [7:0] Ent__A,
  input  [7:0] Ent__B,
  output [7:0] Soma,
  output C__Out
);

  wire sum1_1_c__out, sum1_2_c__out, sum1_3_c__out, sum1_4_c__out, sum1_5_c__out, sum1_6_c__out,
       sum1_7_c__out;

  Sum1 sum1_1 (.C__In(C__In), .Bit_A(Ent__A[0]), .Bit_B(Ent__B[0]), .soma(Soma[0]), .C__Out(sum1_1_c__out));
  Sum1 sum1_2 (.C__In(sum1_1_c__out), .Bit_A(Ent__A[1]), .Bit_B(Ent__B[1]), .soma(Soma[1]), .C__Out(sum1_2_c__out));
  Sum1 sum1_3 (.C__In(sum1_2_c__out), .Bit_A(Ent__A[2]), .Bit_B(Ent__B[2]), .soma(Soma[2]), .C__Out(sum1_3_c__out));
  Sum1 sum1_4 (.C__In(sum1_3_c__out), .Bit_A(Ent__A[3]), .Bit_B(Ent__B[3]), .soma(Soma[3]), .C__Out(sum1_4_c__out));
  Sum1 sum1_5 (.C__In(sum1_4_c__out), .Bit_A(Ent__A[4]), .Bit_B(Ent__B[4]), .soma(Soma[4]), .C__Out(sum1_5_c__out));
  Sum1 sum1_6 (.C__In(sum1_5_c__out), .Bit_A(Ent__A[5]), .Bit_B(Ent__B[5]), .soma(Soma[5]), .C__Out(sum1_6_c__out));
  Sum1 sum1_7 (.C__In(sum1_6_c__out), .Bit_A(Ent__A[6]), .Bit_B(Ent__B[6]), .soma(Soma[6]), .C__Out(sum1_7_c__out));
  Sum1 sum1_8 (.C__In(sum1_7_c__out), .Bit_A(Ent__A[7]), .Bit_B(Ent__B[7]), .soma(Soma[7]), .C__Out(C__Out));
endmodule

// 1Bit
module Mem1 (
  input  Input,
  input  Set,
  output out_3
);

  wire nand_1_out, nand_2_out, nand_4_out;

  nand nand_1 (nand_1_out, Input, Set);
  nand nand_2 (nand_2_out, nand_1_out, Set);
  nand nand_3 (out_3, nand_1_out, nand_4_out);
  nand nand_4 (nand_4_out, out_3, nand_2_out);

  // Notes on the sheet:
  //   Enable
endmodule

module Reg8 (
  input  [7:0] in_1,
  input  in_2,
  input  in_3,
  output [7:0] out_4
);

  wire mem1_1_out_3, mem1_2_out_3, mem1_3_out_3, mem1_4_out_3, mem1_5_out_3, mem1_6_out_3, mem1_7_out_3,
       mem1_8_out_3;

  Mem1 mem1_1 (.Input(in_1[0]), .Set(in_2), .out_3(mem1_1_out_3));
  Mem1 mem1_2 (.Input(in_1[1]), .Set(in_2), .out_3(mem1_2_out_3));
  Mem1 mem1_3 (.Input(in_1[2]), .Set(in_2), .out_3(mem1_3_out_3));
  Mem1 mem1_4 (.Input(in_1[3]), .Set(in_2), .out_3(mem1_4_out_3));
  Mem1 mem1_5 (.Input(in_1[4]), .Set(in_2), .out_3(mem1_5_out_3));
  Mem1 mem1_6 (.Input(in_1[5]), .Set(in_2), .out_3(mem1_6_out_3));
  Mem1 mem1_7 (.Input(in_1[6]), .Set(in_2), .out_3(mem1_7_out_3));
  Mem1 mem1_8 (.Input(in_1[7]), .Set(in_2), .out_3(mem1_8_out_3));
  and and_1 (out_4[0], in_3, mem1_1_out_3);
  and and_2 (out_4[1], in_3, mem1_2_out_3);
  and and_3 (out_4[2], in_3, mem1_3_out_3);
  and and_4 (out_4[3], in_3, mem1_4_out_3);
  and and_5 (out_4[4], in_3, mem1_5_out_3);
  and and_6 (out_4[5], in_3, mem1_6_out_3);
  and and_7 (out_4[6], in_3, mem1_7_out_3);
  and and_8 (out_4[7], in_3, mem1_8_out_3);
endmodule

// R
module Rg2 (
  input  [7:0] in_1,
  input  in_2,
  input  in_3,
  output [7:0] out_4
);

  wire [7:0] register_1_q;

  Register register_1 (.D(in_1), .Q(register_1_q), .clk(in_2));  // open: en, clr
  assign out_4 = in_3 ? register_1_q : 8'bz;  // Controlled_Buffer controlled_buffer_1
endmodule

module RgFire (
  input  [7:0] in_1,
  input  WE,
  input  [1:0] in_3,
  input  in_4,
  input  in_5,
  input  in_6,
  input  in_7,
  input  in_8,
  input  in_9,
  input  in_10,
  input  in_11
);

  wire and_1_out, and_2_out, and_3_out, and_4_out, decoder_1_out0, decoder_1_out1, decoder_1_out2,
       decoder_1_out3;

  Decoder #(.select(2)) decoder_1 (
    .out0(decoder_1_out0), .out1(decoder_1_out1), .out2(decoder_1_out2), .out3(decoder_1_out3), .sel(in_3));  // open: en
  Rg2 rg2_1 (.in_1(in_1), .in_2(and_1_out), .out_4(in_1));  // open: in_3
  and and_1 (and_1_out, decoder_1_out0, WE);
  and and_2 (and_2_out, decoder_1_out1, WE);
  Rg2 rg2_2 (.in_1(in_1), .in_2(and_2_out), .out_4(in_1));  // open: in_3
  Rg2 rg2_3 (.in_1(in_1), .in_2(and_3_out), .out_4(in_1));  // open: in_3
  and and_3 (and_3_out, decoder_1_out2, WE);
  and and_4 (and_4_out, decoder_1_out3, WE);
  Rg2 rg2_4 (.in_1(in_1), .in_2(and_4_out), .out_4(in_1));  // open: in_3

  // Notes on the sheet:
  //   Data
  //   AD
  //   Top     instruct         op1        op2
endmodule

// Cel
module Mem8 (
  input  [7:0] in_1,
  input  in_2,
  input  in_3,
  input  S,
  input  E,
  output [7:0] out_6
);

  wire and_1_out, and_2_out, and_3_out;

  and and_1 (and_1_out, in_2, in_3);
  and and_2 (and_2_out, and_1_out, S);
  and and_3 (and_3_out, and_1_out, E);
  Reg8 reg8_1 (.in_1(in_1), .in_2(and_2_out), .in_3(and_3_out), .out_4(out_6));
endmodule

module Mem16 (
  input  [7:0] ADD,
  input  in_2,
  input  [7:0] Data,
  input  WE,
  input  CLK,
  output [7:0] no_Barramento
);

  wire and_1_out, and_2_out, and_3_out, and_4_out, and_5_out, and_6_out, and_7_out, and_8_out, and_9_out,
       and_10_out, and_11_out, and_12_out, and_13_out, and_14_out, and_15_out, and_16_out, and_17_out,
       and_18_out, and_19_out, and_20_out, and_21_out, and_22_out, and_23_out, and_24_out, and_25_out,
       and_26_out, and_27_out, and_28_out, and_29_out, and_30_out, and_31_out, and_32_out, and_33_out,
       and_34_out, and_35_out, and_36_out, and_37_out, and_38_out, and_39_out, and_40_out, and_41_out,
       and_42_out, and_43_out, and_44_out, and_45_out, and_46_out, and_47_out, and_48_out, and_49_out,
       and_50_out, and_51_out, and_52_out, and_53_out, and_54_out, and_55_out, and_56_out, and_57_out,
       and_58_out, and_59_out, and_60_out, and_61_out, and_62_out, and_63_out, and_64_out, decoder_1_out0,
       decoder_1_out1, decoder_1_out2, decoder_1_out3, decoder_2_out0, decoder_2_out1, decoder_2_out2,
       decoder_2_out3;
  wire [3:0] register_1_q, register_1_q_2;
  wire [7:0] register_2_q, register_3_q, register_4_q, register_5_q, register_6_q, register_7_q,
       register_8_q, register_9_q, register_10_q, register_11_q, register_12_q, register_13_q, register_14_q,
       register_15_q, register_16_q, register_17_q;

  Register register_1 (.D(ADD), .Q({register_1_q_2, register_1_q}), .clk(in_2));  // open: en, clr
  Decoder #(.enable("false"), .select(4)) decoder_1 (
    .out0(decoder_1_out0), .out1(decoder_1_out1), .out2(decoder_1_out2), .out3(decoder_1_out3),
    .sel(register_1_q));  // open: out4, out5, out6, out7, out8, out9, out10, out11, out12, out13, out14, out15
  Decoder #(.enable("false"), .select(4)) decoder_2 (
    .out0(decoder_2_out0), .out1(decoder_2_out1), .out2(decoder_2_out2), .out3(decoder_2_out3),
    .sel(register_1_q_2));  // open: out4, out5, out6, out7, out8, out9, out10, out11, out12, out13, out14, out15
  assign no_Barramento = WE ? Data : 8'bz;  // Controlled_Buffer controlled_buffer_1
  and and_1 (and_1_out, decoder_2_out0, decoder_1_out0);
  and and_2 (and_2_out, and_1_out, WE);
  and and_3 (and_3_out, and_1_out, CLK);
  and and_4 (and_4_out, decoder_2_out1, decoder_1_out0);
  and and_5 (and_5_out, and_4_out, WE);
  and and_6 (and_6_out, and_4_out, CLK);
  and and_7 (and_7_out, decoder_2_out2, decoder_1_out0);
  and and_8 (and_8_out, and_7_out, WE);
  and and_9 (and_9_out, and_7_out, CLK);
  and and_10 (and_10_out, decoder_2_out3, decoder_1_out0);
  and and_11 (and_11_out, and_10_out, WE);
  and and_12 (and_12_out, and_10_out, CLK);
  Register register_2 (.D(no_Barramento), .en(and_2_out), .Q(register_2_q), .clk(and_3_out));  // open: clr
  Register register_3 (.D(no_Barramento), .en(and_5_out), .Q(register_3_q), .clk(and_6_out));  // open: clr
  Register register_4 (.D(no_Barramento), .en(and_8_out), .Q(register_4_q), .clk(and_9_out));  // open: clr
  Register register_5 (.D(no_Barramento), .en(and_11_out), .Q(register_5_q), .clk(and_12_out));  // open: clr
  and and_13 (and_13_out, and_1_out, CLK);
  assign no_Barramento = and_13_out ? register_2_q : 8'bz;  // Controlled_Buffer controlled_buffer_2
  and and_14 (and_14_out, and_4_out, CLK);
  assign no_Barramento = and_14_out ? register_3_q : 8'bz;  // Controlled_Buffer controlled_buffer_3
  and and_15 (and_15_out, and_7_out, CLK);
  assign no_Barramento = and_15_out ? register_4_q : 8'bz;  // Controlled_Buffer controlled_buffer_4
  and and_16 (and_16_out, and_10_out, CLK);
  assign no_Barramento = and_16_out ? register_5_q : 8'bz;  // Controlled_Buffer controlled_buffer_5
  and and_17 (and_17_out, decoder_2_out0, decoder_1_out1);
  and and_18 (and_18_out, decoder_2_out1, decoder_1_out1);
  and and_19 (and_19_out, decoder_2_out2, decoder_1_out1);
  and and_20 (and_20_out, decoder_2_out3, decoder_1_out1);
  and and_21 (and_21_out, and_17_out, WE);
  Register register_6 (.D(no_Barramento), .en(and_21_out), .Q(register_6_q), .clk(and_22_out));  // open: clr
  and and_22 (and_22_out, and_17_out, CLK);
  and and_23 (and_23_out, and_18_out, WE);
  Register register_7 (.D(no_Barramento), .en(and_23_out), .Q(register_7_q), .clk(and_24_out));  // open: clr
  and and_24 (and_24_out, and_18_out, CLK);
  and and_25 (and_25_out, and_19_out, WE);
  Register register_8 (.D(no_Barramento), .en(and_25_out), .Q(register_8_q), .clk(and_26_out));  // open: clr
  and and_26 (and_26_out, and_19_out, CLK);
  and and_27 (and_27_out, and_20_out, WE);
  Register register_9 (.D(no_Barramento), .en(and_27_out), .Q(register_9_q), .clk(and_28_out));  // open: clr
  and and_28 (and_28_out, and_20_out, CLK);
  and and_29 (and_29_out, and_17_out, CLK);
  assign no_Barramento = and_29_out ? register_6_q : 8'bz;  // Controlled_Buffer controlled_buffer_6
  and and_30 (and_30_out, and_18_out, CLK);
  assign no_Barramento = and_30_out ? register_7_q : 8'bz;  // Controlled_Buffer controlled_buffer_7
  and and_31 (and_31_out, and_19_out, CLK);
  assign no_Barramento = and_31_out ? register_8_q : 8'bz;  // Controlled_Buffer controlled_buffer_8
  and and_32 (and_32_out, and_20_out, CLK);
  assign no_Barramento = and_32_out ? register_9_q : 8'bz;  // Controlled_Buffer controlled_buffer_9
  and and_33 (and_33_out, decoder_2_out0, decoder_1_out2);
  and and_34 (and_34_out, decoder_2_out1, decoder_1_out2);
  and and_35 (and_35_out, decoder_2_out2, decoder_1_out2);
  and and_36 (and_36_out, decoder_2_out3, decoder_1_out2);
  and and_37 (and_37_out, and_33_out, WE);
  and and_38 (and_38_out, and_33_out, CLK);
  and and_39 (and_39_out, and_34_out, WE);
  and and_40 (and_40_out, and_34_out, CLK);
  and and_41 (and_41_out, and_35_out, WE);
  and and_42 (and_42_out, and_35_out, CLK);
  and and_43 (and_43_out, and_36_out, WE);
  and and_44 (and_44_out, and_36_out, CLK);
  Register register_10 (.D(no_Barramento), .en(and_37_out), .Q(register_10_q), .clk(and_38_out));  // open: clr
  and and_45 (and_45_out, and_33_out, CLK);
  assign no_Barramento = and_45_out ? register_10_q : 8'bz;  // Controlled_Buffer controlled_buffer_10
  Register register_11 (.D(no_Barramento), .en(and_39_out), .Q(register_11_q), .clk(and_40_out));  // open: clr
  and and_46 (and_46_out, and_34_out, CLK);
  assign no_Barramento = and_46_out ? register_11_q : 8'bz;  // Controlled_Buffer controlled_buffer_11
  Register register_12 (.D(no_Barramento), .en(and_41_out), .Q(register_12_q), .clk(and_42_out));  // open: clr
  and and_47 (and_47_out, and_35_out, CLK);
  assign no_Barramento = and_47_out ? register_12_q : 8'bz;  // Controlled_Buffer controlled_buffer_12
  Register register_13 (.D(no_Barramento), .en(and_43_out), .Q(register_13_q), .clk(and_44_out));  // open: clr
  and and_48 (and_48_out, and_36_out, CLK);
  assign no_Barramento = and_48_out ? register_13_q : 8'bz;  // Controlled_Buffer controlled_buffer_13
  and and_49 (and_49_out, decoder_2_out0, decoder_1_out3);
  and and_50 (and_50_out, and_49_out, WE);
  and and_51 (and_51_out, and_49_out, CLK);
  and and_52 (and_52_out, decoder_2_out1, decoder_1_out3);
  and and_53 (and_53_out, and_52_out, WE);
  and and_54 (and_54_out, and_52_out, CLK);
  and and_55 (and_55_out, decoder_2_out2, decoder_1_out3);
  and and_56 (and_56_out, and_55_out, WE);
  and and_57 (and_57_out, and_55_out, CLK);
  and and_58 (and_58_out, decoder_2_out3, decoder_1_out3);
  and and_59 (and_59_out, and_58_out, WE);
  and and_60 (and_60_out, and_58_out, CLK);
  Register register_14 (.D(no_Barramento), .en(and_50_out), .Q(register_14_q), .clk(and_51_out));  // open: clr
  and and_61 (and_61_out, and_49_out, CLK);
  Register register_15 (.D(no_Barramento), .en(and_53_out), .Q(register_15_q), .clk(and_54_out));  // open: clr
  and and_62 (and_62_out, and_52_out, CLK);
  Register register_16 (.D(no_Barramento), .en(and_56_out), .Q(register_16_q), .clk(and_57_out));  // open: clr
  and and_63 (and_63_out, and_55_out, CLK);
  Register register_17 (.D(no_Barramento), .en(and_59_out), .Q(register_17_q), .clk(and_60_out));  // open: clr
  and and_64 (and_64_out, and_58_out, CLK);
  assign no_Barramento = and_61_out ? register_14_q : 8'bz;  // Controlled_Buffer controlled_buffer_14
  assign no_Barramento = and_62_out ? register_15_q : 8'bz;  // Controlled_Buffer controlled_buffer_15
  assign no_Barramento = and_63_out ? register_16_q : 8'bz;  // Controlled_Buffer controlled_buffer_16
  assign no_Barramento = and_64_out ? register_17_q : 8'bz;  // Controlled_Buffer controlled_buffer_17

  // Notes on the sheet:
  //   MAR
  //   Dado Atual
  //   WE "1" - gravação
  //   WE "0" - leitura
endmodule

// Ula
module ULA (
  input  [2:0] Sel_ULA,
  input  [7:0] EntA_ULA,
  input  [7:0] EntB_ULA,
  input  Bus_1,
  input  C_in,
  output C_out,
  output [7:0] ACC,
  output a_larger,
  output equal,
  output zero
);

  wire adder_1_cout, and_2_out, shift_l_1_out_4, shift_r_1_out_4;
  wire [7:0] adder_1_out, and_1_out, not_1_out, or_1_out, shift_l_1_out_3, shift_r_1_out_3, xor_1_out;

  Adder adder_1 (.a(EntA_ULA), .b(EntB_ULA), .out(adder_1_out), .cin(and_2_out), .cout(adder_1_cout));
  shift_r shift_r_1 (.in_2(EntB_ULA), .in_1(and_2_out), .out_4(shift_r_1_out_4), .out_3(shift_r_1_out_3));
  shift_l shift_l_1 (.in_2(EntB_ULA), .in_1(and_2_out), .out_4(shift_l_1_out_4), .out_3(shift_l_1_out_3));
  assign not_1_out = ~EntA_ULA;  // NOT_Gate not_1, 8 bits wide
  assign and_1_out = EntA_ULA & EntB_ULA;  // AND_Gate and_1, 8 bits wide
  assign or_1_out = EntA_ULA | EntB_ULA;  // OR_Gate or_1, 8 bits wide
  assign xor_1_out = EntA_ULA ^ EntB_ULA;  // XOR_Gate xor_1, 8 bits wide
  Comparator comparator_1 (.a(EntA_ULA), .b(EntB_ULA), .gt(a_larger), .eq(equal));  // open: lt
  Multiplexer #(.enable("true"), .select(3), .width(8)) multiplexer_1 (
    .in0(adder_1_out), .in1(shift_r_1_out_3), .in2(shift_l_1_out_3), .in3(not_1_out), .in4(and_1_out),
    .in5(or_1_out), .in6(xor_1_out), .in7({8{1'b0}}), .out(ACC), .sel(Sel_ULA));  // open: en
  Multiplexer #(.select(3)) multiplexer_2 (
    .in0(adder_1_cout), .in1(shift_r_1_out_4), .in2(shift_l_1_out_4), .in3(1'b0), .in4(1'b0), .in5(1'b0),
    .in6(1'b0), .in7(1'b0), .out(C_out), .sel(Sel_ULA));
  Comparator comparator_2 (.a(ACC), .b({8{1'b0}}), .eq(zero));  // open: gt, lt
  and and_2 (and_2_out, ~Bus_1, C_in);  // AND_Gate

  // Notes on the sheet:
  //   C. Out
endmodule

// Sh_l
module shift_l (
  input  in_1,
  input  [7:0] in_2,
  output [7:0] out_3,
  output out_4
);


  assign out_3 = {in_2[6:0], in_1};
  assign out_4 = in_2[7];
endmodule

// Sh_r
module shift_r (
  input  in_1,
  input  [7:0] in_2,
  output [7:0] out_3,
  output out_4
);


  assign out_3 = {in_1, in_2[7:1]};
  assign out_4 = in_2[0];
endmodule

module UC (
  input  carry_out,
  input  a_larger,
  input  equal,
  input  zero,
  input  [7:0] Ent_IR,
  output Bus_1,
  output TMP_s,
  output R0_s,
  output R0_e,
  output R1_s,
  output R1_e,
  output R2_s,
  output R2_e,
  output R3_s,
  output R3_e,
  output MAR_s,
  output [2:0] Sel_ULA,
  output Init,
  output Flags_s,
  output ACC_s,
  output ACC_e,
  output IAR_s,
  output IAR_e,
  output IR_s,
  output IO_s,
  output IO_e,
  output Data_adress,
  output Input_Output,
  output RAM_e,
  output RAM_s
);

  wire and_5_out, and_6_out, and_7_out, and_8_out, and_9_out, and_10_out, and_11_out, and_12_out, and_16_out,
       and_17_out, and_18_out, and_19_out, and_20_out, and_21_out, and_22_out, and_23_out, and_24_out,
       and_25_out, and_26_out, and_27_out, and_28_out, and_29_out, and_30_out, and_31_out, and_32_out,
       and_33_out, and_34_out, and_35_out, and_36_out, and_37_out, and_38_out, and_39_out, clk_1_clk1,
       clk_1_clk_e, clk_1_clk_s, decoder_1_out0, decoder_1_out1, decoder_1_out2, decoder_1_out3,
       decoder_1_out4, decoder_1_out5, decoder_1_out6, decoder_1_out7, decoder_2_out0, decoder_2_out1,
       decoder_2_out2, decoder_2_out3, decoder_3_out0, decoder_3_out1, decoder_3_out2, decoder_3_out3,
       decoder_4_out0, decoder_4_out1, decoder_4_out2, decoder_4_out3, not_1_out, not_2_out, not_3_out,
       or_6_out, or_7_out, or_8_out, or_9_out, or_10_out, or_11_out, or_12_out, or_13_out, or_14_out,
       or_15_out, or_16_out, steper_1_out_3, steper_1_out_4, steper_1_out_5, steper_1_out_6, steper_1_out_7,
       steper_1_out_8;

  clk clk_1 (.clk_s(clk_1_clk_s), .clk1(clk_1_clk1), .clk_e(clk_1_clk_e));
  or or_1 (R0_e, and_5_out, and_9_out);
  or or_2 (R1_e, and_6_out, and_10_out);
  or or_3 (R2_e, and_7_out, and_11_out);
  or or_4 (R3_e, and_8_out, and_12_out);
  and and_1 (IAR_e, clk_1_clk_e, or_6_out);
  and and_2 (RAM_e, clk_1_clk_e, or_7_out);
  and and_3 (ACC_e, clk_1_clk_e, or_8_out);
  and and_4 (IO_e, clk_1_clk_e, and_36_out);
  and and_5 (and_5_out, clk_1_clk_e, or_9_out, decoder_2_out0);
  and and_6 (and_6_out, clk_1_clk_e, or_9_out, decoder_2_out1);
  and and_7 (and_7_out, clk_1_clk_e, or_9_out, decoder_2_out2);
  and and_8 (and_8_out, clk_1_clk_e, or_9_out, decoder_2_out3);
  and and_9 (and_9_out, clk_1_clk_e, or_10_out, decoder_3_out0);
  and and_10 (and_10_out, clk_1_clk_e, or_10_out, decoder_3_out1);
  and and_11 (and_11_out, clk_1_clk_e, or_10_out, decoder_3_out2);
  and and_12 (and_12_out, clk_1_clk_e, or_10_out, decoder_3_out3);
  or or_5 (Bus_1, steper_1_out_3, and_23_out, and_22_out, and_19_out);
  or or_6 (or_6_out, steper_1_out_3, and_19_out, and_21_out, and_22_out);
  or or_7 (or_7_out, steper_1_out_4, and_39_out, and_34_out, and_33_out, and_31_out);
  or or_8 (or_8_out, steper_1_out_5, and_35_out, and_38_out, and_37_out);
  or or_9 (or_9_out, and_16_out, and_32_out, and_20_out, and_24_out);
  or or_10 (or_10_out, and_18_out, and_17_out, and_30_out);
  Decoder #(.select(3)) decoder_1 (
    .out0(decoder_1_out0), .out1(decoder_1_out1), .out2(decoder_1_out2), .out3(decoder_1_out3),
    .out4(decoder_1_out4), .out5(decoder_1_out5), .out6(decoder_1_out6), .out7(decoder_1_out7),
    .sel(Ent_IR[6:4]), .en(not_1_out));
  Decoder #(.enable("false"), .select(2)) decoder_2 (
    .out0(decoder_2_out0), .out1(decoder_2_out1), .out2(decoder_2_out2), .out3(decoder_2_out3),
    .sel(Ent_IR[1:0]));
  Decoder #(.enable("false"), .select(2)) decoder_3 (
    .out0(decoder_3_out0), .out1(decoder_3_out1), .out2(decoder_3_out2), .out3(decoder_3_out3),
    .sel(Ent_IR[3:2]));
  and and_13 (Sel_ULA[0], steper_1_out_7, Ent_IR[4], Ent_IR[7]);
  and and_14 (Sel_ULA[1], steper_1_out_7, Ent_IR[5], Ent_IR[7]);
  and and_15 (Sel_ULA[2], steper_1_out_7, Ent_IR[6], Ent_IR[7]);
  not not_1 (not_1_out, Ent_IR[7]);
  Steper steper_1 (
    .in_1(clk_1_clk1), .out_3(steper_1_out_3), .out_4(steper_1_out_4), .out_5(steper_1_out_5),
    .out_6(steper_1_out_6), .out_7(steper_1_out_7), .out_8(steper_1_out_8), .out_2(Init));
  and and_16 (and_16_out, steper_1_out_6, Ent_IR[7]);
  and and_17 (and_17_out, steper_1_out_6, decoder_1_out0);
  and and_18 (and_18_out, steper_1_out_6, decoder_1_out1);
  and and_19 (and_19_out, steper_1_out_6, decoder_1_out2);
  and and_20 (and_20_out, steper_1_out_6, decoder_1_out3);
  and and_21 (and_21_out, steper_1_out_6, decoder_1_out4);
  and and_22 (and_22_out, steper_1_out_6, decoder_1_out5);
  and and_23 (and_23_out, steper_1_out_6, decoder_1_out6);
  and and_24 (and_24_out, steper_1_out_6, decoder_1_out7, Ent_IR[3]);
  and and_25 (and_25_out, Ent_IR[3], carry_out);
  and and_26 (and_26_out, Ent_IR[2], a_larger);
  and and_27 (and_27_out, Ent_IR[1], equal);
  and and_28 (and_28_out, Ent_IR[0], zero);
  and and_29 (and_29_out, Ent_IR[4], Ent_IR[5], Ent_IR[6]);
  not not_2 (not_2_out, Ent_IR[3]);
  not not_3 (not_3_out, and_29_out);
  and and_30 (and_30_out, steper_1_out_7, Ent_IR[7]);
  and and_31 (and_31_out, steper_1_out_7, decoder_1_out0);
  and and_32 (and_32_out, steper_1_out_7, decoder_1_out1);
  and and_33 (and_33_out, steper_1_out_7, decoder_1_out2);
  and and_34 (and_34_out, steper_1_out_7, decoder_1_out4);
  and and_35 (and_35_out, steper_1_out_7, decoder_1_out5);
  and and_36 (and_36_out, steper_1_out_7, decoder_1_out7, not_2_out);
  or or_11 (or_11_out, and_25_out, and_26_out, and_27_out, and_28_out);
  and and_37 (and_37_out, steper_1_out_8, Ent_IR[7], not_3_out);
  and and_38 (and_38_out, steper_1_out_8, decoder_1_out2);
  and and_39 (and_39_out, steper_1_out_8, decoder_1_out5, or_11_out);
  or or_12 (or_12_out, and_23_out, and_30_out);
  Decoder #(.enable("false"), .select(2)) decoder_4 (
    .out0(decoder_4_out0), .out1(decoder_4_out1), .out2(decoder_4_out2), .out3(decoder_4_out3),
    .sel(Ent_IR[1:0]));
  or or_13 (or_13_out, steper_1_out_3, and_19_out, and_22_out, and_17_out, and_18_out, and_21_out);
  or or_14 (or_14_out, steper_1_out_5, and_20_out, and_34_out, and_35_out, and_38_out, and_39_out);
  or or_15 (or_15_out, steper_1_out_3, and_19_out, and_22_out, and_30_out);
  or or_16 (or_16_out, and_31_out, and_37_out, and_33_out, and_36_out);
  and and_40 (IR_s, clk_1_clk_s, steper_1_out_4);
  and and_41 (MAR_s, clk_1_clk_s, or_13_out);
  and and_42 (IAR_s, clk_1_clk_s, or_14_out);
  and and_43 (ACC_s, clk_1_clk_s, or_15_out);
  and and_44 (RAM_s, clk_1_clk_s, and_32_out);
  and and_45 (TMP_s, clk_1_clk_s, and_16_out);
  and and_46 (Flags_s, clk_1_clk_s, or_12_out);
  and and_47 (IO_s, clk_1_clk_s, and_24_out);
  and and_48 (R0_s, clk_1_clk_s, or_16_out, decoder_4_out0);
  and and_49 (R1_s, clk_1_clk_s, or_16_out, decoder_4_out1);
  and and_50 (R2_s, clk_1_clk_s, or_16_out, decoder_4_out2);
  and and_51 (R3_s, clk_1_clk_s, or_16_out, decoder_4_out3);

  assign Data_adress = Ent_IR[2];
  assign Input_Output = Ent_IR[3];

  // Other names for the same wires on the sheet: IR[7:0] = Ent_IR; A = a_larger; C = carry_out; E = equal; Z = zero

  // Notes on the sheet:
  //   ENABLEs
  //   SETs
endmodule

module clk (
  output clk_s,
  output clk1,
  output clk_e
);

  wire clock_2_out;

  Clock #(.highDuration(2), .lowDuration(2)) clock_1 (.out(clk1));
  Clock #(.highDuration(2), .lowDuration(2), .phaseOffset(3)) clock_2 (.out(clock_2_out));
  or or_1 (clk_e, clk1, clock_2_out);
  and and_1 (clk_s, clk1, clock_2_out);

  // Notes on the sheet:
  //   clk_d
endmodule

// Steps
module Steper (
  input  in_1,
  output out_2,
  output out_3,
  output out_4,
  output out_5,
  output out_6,
  output out_7,
  output out_8
);

  wire decoder_1_out7;
  wire [2:0] counter_1_q;

  Counter #(.max('h7), .width(3)) counter_1 (
    .D(counter_1_q), .Q(counter_1_q), .clk(in_1), .clr(decoder_1_out7));  // open: load, count, carry, up
  Decoder #(.enable("false"), .select(3)) decoder_1 (
    .out0(out_2), .out1(out_3), .out2(out_4), .out3(out_5), .out4(out_6), .out5(out_7), .out6(out_8),
    .out7(decoder_1_out7), .sel(counter_1_q));
endmodule

module IR (
  input  set,
  input  [7:0] dado_barramento,
  output out_3,
  output out_4,
  output out_5,
  output out_6,
  output out_7,
  output out_8,
  output out_9,
  output out_10
);

  Register register_1 (
    .D(dado_barramento), .en(set), .Q({out_3, out_4, out_5, out_6, out_7, out_8, out_9, out_10}));  // open: clk, clr
endmodule

// caez
module Flags_Caez (
  input  C_out,
  input  a_larger,
  input  equal,
  input  zero,
  input  Flags_s,
  output C,
  output A,
  output E,
  output Z
);

  Register #(.width(4)) register_1 (
    .D({zero, equal, a_larger, C_out}), .Q({Z, E, A, C}), .clk(Flags_s));  // open: en, clr
endmodule

// controle
module Monitor_control (
  input  [7:0] Data_Output,
  input  IO_s,
  input  D_adr,
  input  I_O,
  output [6:0] Data_Monitor,
  output Monitor_set,
  output Monitor_write_enable
);

  wire and_1_out, comparator_1_eq;

  Comparator comparator_1 (.a(Data_Output), .b(8'h80), .eq(comparator_1_eq));  // open: gt, lt
  and and_1 (and_1_out, IO_s, D_adr, I_O);
  and and_2 (Monitor_set, IO_s, ~D_adr, I_O);  // AND_Gate
  Bit_Extender #(.out_width(7)) bit_extender_1 (.in(Data_Output), .out(Data_Monitor));
  Register #(.width(1)) register_1 (.D(comparator_1_eq), .Q(Monitor_write_enable), .clk(and_1_out));  // open: en, clr
endmodule

module keyboard_control (
  input  [7:0] in_1,
  input  init,
  input  [6:0] key,
  input  IO_s,
  input  O_A,
  input  I_O,
  output [7:0] out_7,
  output out_8,
  output out_9
);

  wire and_1_out, comparator_1_eq;
  wire [7:0] bit_extender_1_out, register_2_q;

  and and_1 (and_1_out, IO_s, O_A, I_O);
  Comparator comparator_1 (.a(in_1), .b(8'h81), .eq(comparator_1_eq));  // open: gt, lt
  T_Flip_Flop t_ff_1 (.T(1'b1), .clk(init), .Q(out_8));  // open: Qn, reset, preset
  Register #(.width(1)) register_1 (.D(comparator_1_eq), .Q(out_9), .clk(and_1_out));  // open: en, clr
  assign bit_extender_1_out = {{1{1'b0}}, key};  // Bit_Extender bit_extender_1
  Register register_2 (.D(bit_extender_1_out), .Q(register_2_q), .clk(init));  // open: en, clr
  assign out_7 = init ? register_2_q : 8'bz;  // Controlled_Buffer controlled_buffer_1
endmodule
