// Logisim project memoria16bits.circ as structural Verilog: 4 circuits, main circuit main
module main (
  input  [7:0] in_1,
  input  in_2,
  input  [1:0] in_3
);

  wire and_1_out, and_2_out, and_3_out, and_4_out, decoder_1_out0, decoder_1_out1, decoder_1_out2,
       decoder_1_out3;

  Decoder #(.select(2)) decoder_1 (
    .out0(decoder_1_out0), .out1(decoder_1_out1), .out2(decoder_1_out2), .out3(decoder_1_out3), .sel(in_3));  // open: en
  and and_1 (and_1_out, decoder_1_out0, in_2);
  R r_1 (.in_1(in_1), .in_2(and_1_out), .out_4(in_1));  // open: in_3
  and and_2 (and_2_out, decoder_1_out1, in_2);
  R r_2 (.in_1(in_1), .in_2(and_2_out), .out_4(in_1));  // open: in_3
  and and_3 (and_3_out, decoder_1_out2, in_2);
  R r_3 (.in_1(in_1), .in_2(and_3_out), .out_4(in_1));  // open: in_3
  and and_4 (and_4_out, decoder_1_out3, in_2);
  R r_4 (.in_1(in_1), .in_2(and_4_out), .out_4(in_1));  // open: in_3
endmodule

module R (
  input  [7:0] in_1,
  input  in_2,
  input  in_3,
  output [7:0] out_4
);

  wire [7:0] register_1_q;

  Register register_1 (.D(in_1), .clk(in_2), .Q(register_1_q));  // open: en, clr
  assign out_4 = in_3 ? register_1_q : 8'bz;  // Controlled_Buffer controlled_buffer_1
endmodule

module memory (
  input  [7:0] in_1,
  input  in_2,
  input  in_3,
  input  in_4,
  input  [7:0] in_5,
  input  in_6
);

  wire decoder_1_out0, decoder_1_out1, decoder_1_out2, decoder_1_out3, decoder_2_out0, decoder_2_out1,
       decoder_2_out2, decoder_2_out3;
  wire [7:0] register_1_q;

  Register register_1 (.D(in_1), .en(in_2), .Q(register_1_q));  // open: clk, clr
  Decoder #(.select(4)) decoder_1 (
    .out0(decoder_1_out0), .out1(decoder_1_out1), .out2(decoder_1_out2), .out3(decoder_1_out3),
    .sel(register_1_q[7:4]));  // open: out4, out5, out6, out7, out8, out9, out10, out11, out12, out13, out14, out15, en
  Decoder #(.select(4)) decoder_2 (
    .out0(decoder_2_out0), .out1(decoder_2_out1), .out2(decoder_2_out2), .out3(decoder_2_out3),
    .sel(register_1_q[3:0]));  // open: out4, out5, out6, out7, out8, out9, out10, out11, out12, out13, out14, out15, en
  memory_cell memory_cell_1 (.in_1(in_5), .a(decoder_1_out0), .b(decoder_2_out0), .c(in_3), .d(in_4), .out_6(in_5));
  memory_cell memory_cell_2 (.in_1(in_5), .a(decoder_1_out1), .b(decoder_2_out0), .c(in_3), .d(in_4), .out_6(in_5));
  memory_cell memory_cell_3 (.in_1(in_5), .a(decoder_1_out2), .b(decoder_2_out0), .c(in_3), .d(in_4), .out_6(in_5));
  memory_cell memory_cell_4 (.in_1(in_5), .a(decoder_1_out3), .b(decoder_2_out0), .c(in_3), .d(in_4), .out_6(in_5));
  memory_cell memory_cell_5 (.in_1(in_5), .a(decoder_1_out0), .b(decoder_2_out1), .c(in_3), .d(in_4), .out_6(in_5));
  memory_cell memory_cell_6 (.in_1(in_5), .a(decoder_1_out1), .b(decoder_2_out1), .c(in_3), .d(in_4), .out_6(in_5));
  memory_cell memory_cell_7 (.in_1(in_5), .a(decoder_1_out2), .b(decoder_2_out1), .c(in_3), .d(in_4), .out_6(in_5));
  memory_cell memory_cell_8 (.in_1(in_5), .a(decoder_1_out3), .b(decoder_2_out1), .c(in_3), .d(in_4), .out_6(in_5));
  memory_cell memory_cell_9 (.in_1(in_5), .a(decoder_1_out0), .b(decoder_2_out2), .c(in_3), .d(in_4), .out_6(in_5));
  memory_cell memory_cell_10 (.in_1(in_5), .a(decoder_1_out1), .b(decoder_2_out2), .c(in_3), .d(in_4), .out_6(in_5));
  memory_cell memory_cell_11 (.in_1(in_5), .a(decoder_1_out2), .b(decoder_2_out2), .c(in_3), .d(in_4), .out_6(in_5));
  memory_cell memory_cell_12 (.in_1(in_5), .a(decoder_1_out3), .b(decoder_2_out2), .c(in_3), .d(in_4), .out_6(in_5));
  memory_cell memory_cell_13 (.in_1(in_5), .a(decoder_1_out0), .b(decoder_2_out3), .c(in_3), .d(in_4), .out_6(in_5));
  memory_cell memory_cell_14 (.in_1(in_5), .a(decoder_1_out1), .b(decoder_2_out3), .c(in_3), .d(in_4), .out_6(in_5));
  memory_cell memory_cell_15 (.in_1(in_5), .a(decoder_1_out2), .b(decoder_2_out3), .c(in_3), .d(in_4), .out_6(in_5));
  memory_cell memory_cell_16 (.in_1(in_5), .a(decoder_1_out3), .b(decoder_2_out3), .c(in_3), .d(in_4), .out_6(in_5));
  Register register_2 (.D(in_5), .clk(in_6));  // open: en, Q, clr
endmodule

module memory_cell (
  input  [7:0] in_1,
  input  a,
  input  b,
  input  c,
  input  d,
  output [7:0] out_6
);

  wire and_1_out, and_2_out, and_3_out;

  and and_1 (and_1_out, a, b);
  and and_2 (and_2_out, and_1_out, c);
  and and_3 (and_3_out, and_1_out, d);
  R r_1 (.in_1(in_1), .in_2(and_2_out), .in_3(and_3_out), .out_4(out_6));
endmodule
