// Logisim project projeto_ULA.circ as structural Verilog: 4 circuits, main circuit main
module main (
  input  [2:0] in_1,
  input  [7:0] in_2,
  input  [7:0] in_3,
  output out_4,
  output out_5,
  output [7:0] out_6,
  output out_7,
  output out_8,
  output out_9,
  output out_10
);

  ULA ula_1 (
    .op(in_1), .entrada_A(in_2), .entrada_B(in_3), .c_in(out_4), .c_out(out_5), .out_6(out_6),
    .larger(out_7), .iqual(out_8), .smaller(out_9), .zero(out_10));
endmodule

module ULA (
  input  [2:0] op,
  input  [7:0] entrada_A,
  input  [7:0] entrada_B,
  output c_in,
  output c_out,
  output [7:0] out_6,
  output larger,
  output iqual,
  output smaller,
  output zero
);

  wire adder_1_cout, left_1_c_out, right_1_c_in;
  wire [7:0] adder_1_out, and_1_out, left_1_saida, not_1_out, or_1_out, right_1_saida, xor_1_out;

  assign not_1_out = ~entrada_A;  // NOT_Gate not_1, 8 bits wide
  assign and_1_out = entrada_A & entrada_B;  // AND_Gate and_1, 8 bits wide
  assign or_1_out = entrada_A | entrada_B;  // OR_Gate or_1, 8 bits wide
  Comparator comparator_1 (.a(entrada_A), .b(entrada_B), .gt(larger), .eq(iqual), .lt(smaller));
  Adder adder_1 (.a(entrada_A), .b(entrada_B), .out(adder_1_out), .cin(c_in), .cout(adder_1_cout));
  assign xor_1_out = entrada_A ^ entrada_B;  // XOR_Gate xor_1, 8 bits wide
  left left_1 (.entrada(entrada_A), .c_in(c_in), .saida(left_1_saida), .c_out(left_1_c_out));
  right right_1 (.entrada(entrada_A), .c_out(c_in), .saida(right_1_saida), .c_in(right_1_c_in));
  Multiplexer #(.select(3), .width(8)) multiplexer_1 (
    .in0(adder_1_out), .in1(left_1_saida), .in2(right_1_saida), .in3(not_1_out), .in4(and_1_out),
    .in5(or_1_out), .in6(xor_1_out), .in7({8{1'b0}}), .out(out_6), .sel(op));
  Comparator comparator_2 (.a(out_6), .b({8{1'b0}}), .eq(zero));  // open: gt, lt
  Multiplexer #(.select(3)) multiplexer_2 (
    .in0(adder_1_cout), .in1(left_1_c_out), .in2(right_1_c_in), .in3(1'b0), .in4(1'b0), .in5(1'b0),
    .in6(1'b0), .in7(1'b0), .out(c_out), .sel(op));
endmodule

module left (
  input  [7:0] entrada,
  output c_in,
  output [7:0] saida,
  output c_out
);


  assign c_out = entrada[7];
  assign saida = {entrada[6:0], c_in};
endmodule

module right (
  input  [7:0] entrada,
  output c_out,
  output [7:0] saida,
  output c_in
);


  assign c_out = entrada[0];
  assign saida = {c_in, entrada[7:1]};
endmodule
